// Logisim project ALU_32_BIT.circ as structural Verilog: 13 circuits, main circuit main
module main (
);

  wire alu_control1_1_alu_src, and_1_out, clock_1_out, comparator_1_eq, control_1_branch, control_1_memread,
       control_1_memtoreg, control_1_memwrite, control_1_regwrite;
  wire [3:0] alu_control1_1_alu_ctrl0;
  wire [31:0] adder_1_out, adder_2_out, alu32bit1_1_result, datamemory_1_readdata, immgen_1_imm32,
       instructionmemory_1_instruction, multiplexer_1_out, multiplexer_2_out, multiplexer_3_out,
       regfile1_1_rdata1, regfile1_1_rdata2, register_1_q;

  Register #(.width(32)) register_1 (
    .D(multiplexer_2_out), .en(1'b1), .clk(clock_1_out), .Q(register_1_q));  // open: clr
  Adder #(.width(32)) adder_1 (.a(register_1_q), .b(32'h4), .out(adder_1_out));  // open: cin, cout
  Clock clock_1 (.out(clock_1_out));
  InstructionMemory instructionmemory_1 (
    .Address(register_1_q[23:0]), .ClockIn(clock_1_out), .Instruction(instructionmemory_1_instruction));
  ImmGen immgen_1 (.Instruction(instructionmemory_1_instruction), .IMM32(immgen_1_imm32));
  Control control_1 (
    .I6_0(instructionmemory_1_instruction[6:0]), .MemtoReg(control_1_memtoreg),
    .RegWrite(control_1_regwrite), .MemRead(control_1_memread), .MemWrite(control_1_memwrite),
    .Branch(control_1_branch));
  RegFile1 regfile1_1 (
    .RReg1(instructionmemory_1_instruction[19:15]), .RReg2(instructionmemory_1_instruction[24:20]),
    .WData(multiplexer_3_out), .Clock_in(clock_1_out), .Write(control_1_regwrite),
    .WReg(instructionmemory_1_instruction[11:7]), .RData1(regfile1_1_rdata1), .RData2(regfile1_1_rdata2));
  ALU_Control1 alu_control1_1 (
    .I30(instructionmemory_1_instruction[30]), .I14(instructionmemory_1_instruction[14]),
    .I13(instructionmemory_1_instruction[13]), .I12(instructionmemory_1_instruction[12]),
    .I6(instructionmemory_1_instruction[6]), .I5(instructionmemory_1_instruction[5]),
    .I4(instructionmemory_1_instruction[4]), .ALU_Ctrl3(alu_control1_1_alu_ctrl0[3]),
    .ALU_Ctrl2(alu_control1_1_alu_ctrl0[2]), .ALU_Ctrl1(alu_control1_1_alu_ctrl0[1]),
    .ALU_Ctrl0(alu_control1_1_alu_ctrl0[0]), .ALU_Src(alu_control1_1_alu_src));
  Multiplexer #(.enable("false"), .width(32)) multiplexer_1 (
    .in0(regfile1_1_rdata2), .in1(immgen_1_imm32), .out(multiplexer_1_out), .sel(alu_control1_1_alu_src));
  Comparator #(.width(32)) comparator_1 (
    .a(regfile1_1_rdata1), .b(regfile1_1_rdata2), .eq(comparator_1_eq));  // open: gt, lt
  Adder #(.width(32)) adder_2 (.a(register_1_q), .b(immgen_1_imm32), .out(adder_2_out));  // open: cin, cout
  and and_1 (and_1_out, control_1_branch, comparator_1_eq);
  Multiplexer #(.enable("false"), .width(32)) multiplexer_2 (
    .in0(adder_1_out), .in1(adder_2_out), .out(multiplexer_2_out), .sel(and_1_out));
  ALU32BIT1 alu32bit1_1 (
    .A(regfile1_1_rdata1), .B(multiplexer_1_out), .ALU_Ctrl(alu_control1_1_alu_ctrl0),
    .Result(alu32bit1_1_result));  // open: C_out
  DataMemory datamemory_1 (
    .Address(alu32bit1_1_result[25:0]), .MemWrite(control_1_memwrite), .MemRead(control_1_memread),
    .ClockIn(clock_1_out), .WriteData(regfile1_1_rdata2), .ReadData(datamemory_1_readdata));
  Multiplexer #(.enable("false"), .width(32)) multiplexer_3 (
    .in0(alu32bit1_1_result), .in1(datamemory_1_readdata), .out(multiplexer_3_out));  // open: sel
endmodule

module Adder1Bit (
  input  A,
  input  B,
  input  Cin,
  output Sum,
  output Cout
);

  wire and_1_out, and_2_out, xor_1_out;

  xor xor_1 (xor_1_out, A, B);
  and and_1 (and_1_out, A, B);
  and and_2 (and_2_out, xor_1_out, Cin);
  xor xor_2 (Sum, xor_1_out, Cin);
  or or_1 (Cout, and_2_out, and_1_out);
endmodule

module Multi (
  input  A,
  input  B,
  input  Select1,
  input  Select0,
  output R
);

  wire and_1_out, and_2_out, and_3_out, and_4_out, not_1_out, not_2_out, not_3_out, not_4_out, or_1_out,
       or_2_out;

  and and_1 (and_1_out, A, B, not_1_out, not_2_out);
  not not_1 (not_1_out, Select1);
  not not_2 (not_2_out, Select0);
  and and_2 (and_2_out, A, B, not_3_out, Select0);
  not not_3 (not_3_out, Select1);
  and and_3 (and_3_out, A, B, Select1, not_4_out);
  not not_4 (not_4_out, Select0);
  and and_4 (and_4_out, A, B, Select1, Select0);
  or or_1 (or_1_out, and_1_out, and_2_out);
  or or_2 (or_2_out, and_3_out, and_4_out);
  or or_3 (R, or_1_out, or_2_out);
endmodule

module ALU1Bit (
  input  A,
  input  B,
  input  Cin,
  input  [3:0] ALU_Ctrl,
  output R,
  output Cout
);

  wire Adder_sum, and_1_out, multiplexer_1_out, not_1_out, or_1_out, xor_1_out;

  Multiplexer #(.enable("false")) multiplexer_1 (.in0(B), .in1(not_1_out), .out(multiplexer_1_out), .sel(ALU_Ctrl[2]));
  not not_1 (not_1_out, B);
  and and_1 (and_1_out, A, multiplexer_1_out);
  or or_1 (or_1_out, A, multiplexer_1_out);
  xor xor_1 (xor_1_out, A, multiplexer_1_out);
  Adder1Bit Adder (.A(A), .B(multiplexer_1_out), .Cin(Cin), .Sum(Adder_sum), .Cout(Cout));
  Multiplexer #(.enable("false"), .select(2)) multiplexer_2 (
    .in0(and_1_out), .in1(or_1_out), .in2(xor_1_out), .in3(Adder_sum), .out(R), .sel(ALU_Ctrl[1:0]));
endmodule

module ALU32Bit (
  input  [31:0] A,
  input  [31:0] B,
  input  [3:0] ALU_Ctrl,
  output [31:0] Result,
  output C_out
);

  wire ALU_0_3_cout, ALU_4_7_cout, ALU_8_11_cout, ALU_12_15_cout, ALU_16_19_cout, ALU_20_23_cout,
       ALU_24_27_cout;

  ALU4BIT ALU_0_3 (.A(A[3:0]), .B(B[3:0]), .ALU_CTRL(ALU_Ctrl), .R(Result[3:0]), .Cout(ALU_0_3_cout));  // open: Cin
  ALU4BIT ALU_4_7 (
    .A(A[7:4]), .B(B[7:4]), .Cin(ALU_0_3_cout), .ALU_CTRL(ALU_Ctrl), .R(Result[7:4]), .Cout(ALU_4_7_cout));
  ALU4BIT ALU_8_11 (
    .A(A[11:8]), .B(B[11:8]), .Cin(ALU_4_7_cout), .ALU_CTRL(ALU_Ctrl), .R(Result[11:8]), .Cout(ALU_8_11_cout));
  ALU4BIT ALU_12_15 (
    .A(A[15:12]), .B(B[15:12]), .Cin(ALU_8_11_cout), .ALU_CTRL(ALU_Ctrl), .R(Result[15:12]),
    .Cout(ALU_12_15_cout));
  ALU4BIT ALU_16_19 (
    .A(A[19:16]), .B(B[19:16]), .Cin(ALU_12_15_cout), .ALU_CTRL(ALU_Ctrl), .R(Result[19:16]),
    .Cout(ALU_16_19_cout));
  ALU4BIT ALU_20_23 (
    .A(A[23:20]), .B(B[23:20]), .Cin(ALU_16_19_cout), .R(Result[23:20]), .Cout(ALU_20_23_cout));  // open: ALU_CTRL
  ALU4BIT ALU_24_27 (
    .A(A[27:24]), .B(B[27:24]), .Cin(ALU_20_23_cout), .ALU_CTRL(ALU_Ctrl), .R(Result[27:24]),
    .Cout(ALU_24_27_cout));
  ALU4BIT ALU_28_31 (
    .A(A[31:28]), .B(B[31:28]), .Cin(ALU_24_27_cout), .ALU_CTRL(ALU_Ctrl), .R(Result[31:28]), .Cout(C_out));

  // Other names for the same wires on the sheet: A_0_3[3:0] = A[3:0]; A_4_7[3:0] = A[7:4]; A_8_11[3:0] = A[11:8];
  //   A_12_15[3:0] = A[15:12]; A_16_19[3:0] = A[19:16]; A_20_23[3:0] = A[23:20]; A_24_27[3:0] = A[27:24];
  //   A_28_31[3:0] = A[31:28]; B_0_3[3:0] = B[3:0]; B_4_7[3:0] = B[7:4]; B_8_11[3:0] = B[11:8];
  //   B_12_15[3:0] = B[15:12]; B_16_19[3:0] = B[19:16]; B_20_23[3:0] = B[23:20]; B_24_27[3:0] = B[27:24];
  //   B_28_31[3:0] = B[31:28]; C = C_out; CTRL[3:0] = ALU_Ctrl; R[31:0] = Result; R_0_3[3:0] = Result[3:0];
  //   R_4_7[3:0] = Result[7:4]; R_8_11[3:0] = Result[11:8]; R_12_15[3:0] = Result[15:12];
  //   R_16_19[3:0] = Result[19:16]; R_20_23[3:0] = Result[23:20]; R_24_27[3:0] = Result[27:24];
  //   R_28_31[3:0] = Result[31:28]
endmodule

module ALU4BIT (
  input  [3:0] A,
  input  [3:0] B,
  input  Cin,
  input  [3:0] ALU_CTRL,
  output [3:0] R,
  output Cout
);

  wire ALU0_cout, ALU1_cout, ALU2_cout;

  ALU1Bit ALU1 (.A(A[1]), .B(B[1]), .Cin(ALU0_cout), .ALU_Ctrl(ALU_CTRL), .R(R[1]), .Cout(ALU1_cout));
  ALU1Bit ALU0 (.A(A[0]), .B(B[0]), .Cin(Cin), .ALU_Ctrl(ALU_CTRL), .R(R[0]), .Cout(ALU0_cout));
  ALU1Bit ALU3 (.A(A[3]), .B(B[3]), .Cin(ALU2_cout), .ALU_Ctrl(ALU_CTRL), .R(R[3]), .Cout(Cout));
  ALU1Bit ALU2 (.A(A[2]), .B(B[2]), .Cin(ALU1_cout), .ALU_Ctrl(ALU_CTRL), .R(R[2]), .Cout(ALU2_cout));
endmodule

module ImmGen (
  input  [31:0] Instruction,
  output [31:0] IMM32
);

  Multiplexer #(.enable("false"), .select(2)) multiplexer_1 (
    .in0(Instruction[20]), .in1(Instruction[7]), .in3(1'b0), .out(IMM32[0]), .sel(Instruction[6:5]));  // open: in2
  Multiplexer #(.enable("false"), .width(4)) multiplexer_2 (
    .in0(Instruction[24:21]), .in1(Instruction[11:8]), .out(IMM32[4:1]), .sel(Instruction[5]));
  Multiplexer #(.enable("false")) multiplexer_3 (
    .in0(Instruction[31]), .in1(Instruction[7]), .out(IMM32[11]), .sel(Instruction[6]));
  assign IMM32[31:12] = {{19{Instruction[31]}}, Instruction[31]};  // Bit_Extender bit_extender_1

  assign IMM32[10:5] = Instruction[30:25];

  // Other names for the same wires on the sheet: I30_25[5:0] = Instruction[30:25]; I5 = Instruction[5];
  //   I6 = Instruction[6]; I7 = Instruction[7]; I11_8[3:0] = Instruction[11:8]; I20 = Instruction[20];
  //   I24_21[3:0] = Instruction[24:21]; I31 = Instruction[31]
endmodule

module RegFile1 (
  input  [4:0] RReg1,
  input  [4:0] RReg2,
  input  [31:0] WData,
  input  Clock_in,
  input  Write,
  input  [4:0] WReg,
  output [31:0] RData1,
  output [31:0] RData2
);

  wire and_1_out, and_2_out, and_3_out, and_4_out, and_5_out, and_6_out, and_7_out, and_8_out, and_9_out,
       and_10_out, and_11_out, and_12_out, and_13_out, and_14_out, and_15_out, and_16_out, and_17_out,
       and_18_out, and_19_out, and_20_out, and_21_out, and_22_out, and_23_out, and_24_out, and_25_out,
       and_26_out, and_27_out, and_28_out, and_29_out, and_30_out, and_31_out, decoder_1_out1,
       decoder_1_out2, decoder_1_out3, decoder_1_out4, decoder_1_out5, decoder_1_out6, decoder_1_out7,
       decoder_1_out8, decoder_1_out9, decoder_1_out10, decoder_1_out11, decoder_1_out12, decoder_1_out13,
       decoder_1_out14, decoder_1_out15, decoder_1_out16, decoder_1_out17, decoder_1_out18, decoder_1_out19,
       decoder_1_out20, decoder_1_out21, decoder_1_out22, decoder_1_out23, decoder_1_out24, decoder_1_out25,
       decoder_1_out26, decoder_1_out27, decoder_1_out28, decoder_1_out29, decoder_1_out30, decoder_1_out31;
  wire [31:0] x0, x1, x2, x3, x4, x5, x6, x7, x8, x9, x10, x11, x12, x13, x14, x15, x16, x17, x18, x19, x20,
       x21, x22, x23, x24, x25, x26, x27, x28, x29, x30, x31;

  Decoder #(.enable("false"), .select(5)) decoder_1 (
    .out1(decoder_1_out1), .out2(decoder_1_out2), .out3(decoder_1_out3), .out4(decoder_1_out4),
    .out5(decoder_1_out5), .out6(decoder_1_out6), .out7(decoder_1_out7), .out8(decoder_1_out8),
    .out9(decoder_1_out9), .out10(decoder_1_out10), .out11(decoder_1_out11), .out12(decoder_1_out12),
    .out13(decoder_1_out13), .out14(decoder_1_out14), .out15(decoder_1_out15), .out16(decoder_1_out16),
    .out17(decoder_1_out17), .out18(decoder_1_out18), .out19(decoder_1_out19), .out20(decoder_1_out20),
    .out21(decoder_1_out21), .out22(decoder_1_out22), .out23(decoder_1_out23), .out24(decoder_1_out24),
    .out25(decoder_1_out25), .out26(decoder_1_out26), .out27(decoder_1_out27), .out28(decoder_1_out28),
    .out29(decoder_1_out29), .out30(decoder_1_out30), .out31(decoder_1_out31), .sel(WReg));  // open: out0
  and and_1 (and_1_out, decoder_1_out1, Write);
  and and_2 (and_2_out, decoder_1_out2, Write);
  and and_3 (and_3_out, decoder_1_out3, Write);
  and and_4 (and_4_out, decoder_1_out4, Write);
  and and_5 (and_5_out, decoder_1_out5, Write);
  and and_6 (and_6_out, decoder_1_out6, Write);
  and and_7 (and_7_out, decoder_1_out7, Write);
  and and_8 (and_8_out, decoder_1_out8, Write);
  and and_9 (and_9_out, decoder_1_out9, Write);
  and and_10 (and_10_out, decoder_1_out10, Write);
  and and_11 (and_11_out, decoder_1_out11, Write);
  and and_12 (and_12_out, decoder_1_out12, Write);
  and and_13 (and_13_out, decoder_1_out13, Write);
  and and_14 (and_14_out, decoder_1_out14, Write);
  and and_15 (and_15_out, decoder_1_out15, Write);
  and and_16 (and_16_out, decoder_1_out16, Write);
  and and_17 (and_17_out, decoder_1_out17, Write);
  and and_18 (and_18_out, decoder_1_out18, Write);
  and and_19 (and_19_out, decoder_1_out19, Write);
  and and_20 (and_20_out, decoder_1_out20, Write);
  and and_21 (and_21_out, decoder_1_out21, Write);
  and and_22 (and_22_out, decoder_1_out22, Write);
  and and_23 (and_23_out, decoder_1_out23, Write);
  and and_24 (and_24_out, decoder_1_out24, Write);
  and and_25 (and_25_out, decoder_1_out25, Write);
  and and_26 (and_26_out, decoder_1_out26, Write);
  and and_27 (and_27_out, decoder_1_out27, Write);
  and and_28 (and_28_out, decoder_1_out28, Write);
  and and_29 (and_29_out, decoder_1_out29, Write);
  and and_30 (and_30_out, decoder_1_out30, Write);
  and and_31 (and_31_out, decoder_1_out31, Write);
  Register #(.width(32)) u_x0 (.Q(x0));  // open: D, en, clk, clr
  Register #(.width(32)) u_x1 (.D(WData), .en(and_1_out), .clk(Clock_in), .Q(x1));  // open: clr
  Register #(.width(32)) u_x2 (.D(WData), .en(and_2_out), .clk(Clock_in), .Q(x2));  // open: clr
  Register #(.width(32)) u_x3 (.D(WData), .en(and_3_out), .clk(Clock_in), .Q(x3));  // open: clr
  Register #(.width(32)) u_x4 (.D(WData), .en(and_4_out), .clk(Clock_in), .Q(x4));  // open: clr
  Register #(.width(32)) u_x5 (.D(WData), .en(and_5_out), .clk(Clock_in), .Q(x5));  // open: clr
  Register #(.width(32)) u_x6 (.D(WData), .en(and_6_out), .clk(Clock_in), .Q(x6));  // open: clr
  Register #(.width(32)) u_x7 (.D(WData), .en(and_7_out), .clk(Clock_in), .Q(x7));  // open: clr
  Register #(.width(32)) u_x8 (.D(WData), .en(and_8_out), .clk(Clock_in), .Q(x8));  // open: clr
  Register #(.width(32)) u_x9 (.D(WData), .en(and_9_out), .clk(Clock_in), .Q(x9));  // open: clr
  Register #(.width(32)) u_x10 (.D(WData), .en(and_10_out), .clk(Clock_in), .Q(x10));  // open: clr
  Register #(.width(32)) u_x11 (.D(WData), .en(and_11_out), .clk(Clock_in), .Q(x11));  // open: clr
  Register #(.width(32)) u_x12 (.D(WData), .en(and_12_out), .clk(Clock_in));  // open: Q, clr
  Register #(.width(32)) u_x13 (.D(WData), .en(and_13_out), .clk(Clock_in));  // open: Q, clr
  Register #(.width(32)) u_x14 (.D(WData), .en(and_14_out), .clk(Clock_in), .Q(x14));  // open: clr
  Register #(.width(32)) u_x15 (.D(WData), .en(and_15_out), .clk(Clock_in), .Q(x15));  // open: clr
  Register #(.width(32)) u_x16 (.D(WData), .en(and_16_out), .clk(Clock_in), .Q(x16));  // open: clr
  Register #(.width(32)) u_x17 (.D(WData), .en(and_17_out), .clk(Clock_in), .Q(x17));  // open: clr
  Register #(.width(32)) u_x18 (.D(WData), .en(and_18_out), .clk(Clock_in), .Q(x18));  // open: clr
  Register #(.width(32)) u_x19 (.D(WData), .en(and_19_out), .clk(Clock_in), .Q(x19));  // open: clr
  Register #(.width(32)) u_x20 (.D(WData), .en(and_20_out), .clk(Clock_in), .Q(x20));  // open: clr
  Register #(.width(32)) u_x21 (.D(WData), .en(and_21_out), .clk(Clock_in), .Q(x21));  // open: clr
  Register #(.width(32)) u_x22 (.D(WData), .en(and_22_out), .clk(Clock_in), .Q(x22));  // open: clr
  Register #(.width(32)) u_x23 (.D(WData), .en(and_23_out), .clk(Clock_in), .Q(x23));  // open: clr
  Register #(.width(32)) u_x24 (.D(WData), .en(and_24_out), .clk(Clock_in), .Q(x24));  // open: clr
  Register #(.width(32)) u_x25 (.D(WData), .en(and_25_out), .clk(Clock_in), .Q(x25));  // open: clr
  Register #(.width(32)) u_x26 (.D(WData), .en(and_26_out), .clk(Clock_in), .Q(x26));  // open: clr
  Register #(.width(32)) u_x27 (.D(WData), .en(and_27_out), .clk(Clock_in), .Q(x27));  // open: clr
  Register #(.width(32)) u_x28 (.D(WData), .en(and_28_out), .clk(Clock_in), .Q(x28));  // open: clr
  Register #(.width(32)) u_x29 (.D(WData), .en(and_29_out), .clk(Clock_in), .Q(x29));  // open: clr
  Register #(.width(32)) u_x30 (.D(WData), .en(and_30_out), .clk(Clock_in), .Q(x30));  // open: clr
  Register #(.width(32)) u_x31 (.D(WData), .en(and_31_out), .clk(Clock_in), .Q(x31));  // open: clr
  Multiplexer #(.enable("false"), .select(5), .width(32)) multiplexer_1 (
    .in1(x1), .in2(x2), .in3(x3), .in4(x4), .in5(x5), .in6(x6), .in7(x7), .in8(x8), .in9(x9), .in10(x10),
    .in11(x11), .in12(x12), .in13(x13), .in14(x14), .in15(x15), .in16(x16), .in17(x17), .in18(x18),
    .in19(x19), .in20(x20), .in21(x21), .in22(x22), .in23(x23), .in24(x24), .in25(x25), .in26(x26),
    .in27(x27), .in28(x28), .in29(x29), .in30(x30), .in31(x31), .out(RData1), .sel(RReg1));  // open: in0
  Multiplexer #(.enable("false"), .select(5), .width(32)) multiplexer_2 (
    .in1(x1), .in2(x2), .in3(x3), .in4(x4), .in5(x5), .in6(x6), .in7(x7), .in8(x8), .in9(x9), .in10(x10),
    .in11(x11), .in12(x12), .in13(x13), .in14(x14), .in15(x15), .in16(x16), .in17(x17), .in18(x18),
    .in19(x19), .in20(x20), .in21(x21), .in22(x22), .in23(x23), .in24(x24), .in25(x25), .in26(x26),
    .in27(x27), .in28(x28), .in29(x29), .in30(x30), .in31(x31), .out(RData2), .sel(RReg2));  // open: in0
endmodule

module ALU_Control1 (
  input  I30,
  input  I14,
  input  I13,
  input  I12,
  input  I6,
  input  I5,
  input  I4,
  output ALU_Ctrl3,
  output ALU_Ctrl2,
  output ALU_Ctrl1,
  output ALU_Ctrl0,
  output ALU_Src
);

  wire and_2_out;

  and and_1 (ALU_Ctrl2, I30, ~I13, I5);  // AND_Gate
  or or_1 (ALU_Ctrl1, ~I13, ~I4);  // OR_Gate
  and and_2 (and_2_out, I13, ~I12);  // AND_Gate
  or or_2 (ALU_Src, ~I5, ~I4);  // OR_Gate
  or or_3 (ALU_Ctrl0, ~I14, and_2_out);  // OR_Gate

  assign ALU_Ctrl3 = 1'b0;

  // Notes on the sheet:
  //   I30_NI13_I5
  //   NI13_OR_NI4
  //   I13_NI12
  //   NI5_OR_NI4
  //   NI14_OR_I13_NI12
endmodule

module ALU32BIT1 (
  input  [31:0] A,
  input  [31:0] B,
  input  [3:0] ALU_Ctrl,
  output [31:0] Result,
  output C_out
);

  wire ALU_0_3_cout, ALU_4_7_cout, ALU_8_11_cout, ALU_12_15_cout, ALU_16_19_cout, ALU_20_23_cout,
       ALU_24_27_cout;

  ALU4BIT ALU_0_3 (.A(A[3:0]), .B(B[3:0]), .ALU_CTRL(ALU_Ctrl), .R(Result[3:0]), .Cout(ALU_0_3_cout));  // open: Cin
  ALU4BIT ALU_4_7 (
    .A(A[7:4]), .B(B[7:4]), .Cin(ALU_0_3_cout), .ALU_CTRL(ALU_Ctrl), .R(Result[7:4]), .Cout(ALU_4_7_cout));
  ALU4BIT ALU_8_11 (
    .A(A[11:8]), .B(B[11:8]), .Cin(ALU_4_7_cout), .ALU_CTRL(ALU_Ctrl), .R(Result[11:8]), .Cout(ALU_8_11_cout));
  ALU4BIT ALU_12_15 (
    .A(A[15:12]), .B(B[15:12]), .Cin(ALU_8_11_cout), .ALU_CTRL(ALU_Ctrl), .R(Result[15:12]),
    .Cout(ALU_12_15_cout));
  ALU4BIT ALU_16_19 (
    .A(A[19:16]), .B(B[19:16]), .Cin(ALU_12_15_cout), .ALU_CTRL(ALU_Ctrl), .R(Result[19:16]),
    .Cout(ALU_16_19_cout));
  ALU4BIT ALU_20_23 (
    .A(A[23:20]), .B(B[23:20]), .Cin(ALU_16_19_cout), .R(Result[23:20]), .Cout(ALU_20_23_cout));  // open: ALU_CTRL
  ALU4BIT ALU_24_27 (
    .A(A[27:24]), .B(B[27:24]), .Cin(ALU_20_23_cout), .ALU_CTRL(ALU_Ctrl), .R(Result[27:24]),
    .Cout(ALU_24_27_cout));
  ALU4BIT ALU_28_31 (
    .A(A[31:28]), .B(B[31:28]), .Cin(ALU_24_27_cout), .ALU_CTRL(ALU_Ctrl), .R(Result[31:28]), .Cout(C_out));

  // Other names for the same wires on the sheet: A_0_3[3:0] = A[3:0]; A_4_7[3:0] = A[7:4]; A_8_11[3:0] = A[11:8];
  //   A_12_15[3:0] = A[15:12]; A_16_19[3:0] = A[19:16]; A_20_23[3:0] = A[23:20]; A_24_27[3:0] = A[27:24];
  //   A_28_31[3:0] = A[31:28]; B_0_3[3:0] = B[3:0]; B_4_7[3:0] = B[7:4]; B_8_11[3:0] = B[11:8];
  //   B_12_15[3:0] = B[15:12]; B_16_19[3:0] = B[19:16]; B_20_23[3:0] = B[23:20]; B_24_27[3:0] = B[27:24];
  //   B_28_31[3:0] = B[31:28]; C = C_out; CTRL[3:0] = ALU_Ctrl; R[31:0] = Result; R_0_3[3:0] = Result[3:0];
  //   R_4_7[3:0] = Result[7:4]; R_8_11[3:0] = Result[11:8]; R_12_15[3:0] = Result[15:12];
  //   R_16_19[3:0] = Result[19:16]; R_20_23[3:0] = Result[23:20]; R_24_27[3:0] = Result[27:24];
  //   R_28_31[3:0] = Result[31:28]
endmodule

module Control (
  input  [6:0] I6_0,
  output MemtoReg,
  output RegWrite,
  output MemRead,
  output MemWrite,
  output Branch
);

  wire not_1_out, not_2_out;

  not not_1 (not_1_out, I6_0[6]);
  not not_2 (not_2_out, I6_0[5]);
  not not_3 (MemtoReg, I6_0[4]);
  or or_1 (RegWrite, not_2_out, I6_0[4]);
  and and_1 (MemRead, not_2_out, MemtoReg);
  and and_2 (MemWrite, not_1_out, I6_0[5], MemtoReg);

  assign Branch = I6_0[6];
endmodule

module DataMemory (
  input  [25:0] Address,
  input  MemWrite,
  input  MemRead,
  input  ClockIn,
  input  [31:0] WriteData,
  output [31:0] ReadData
);

  wire MR0, MR1, MR2, MR3, MW0, MW1, MW2, MW3;
  wire [31:0] D1, D2, D3, ram_1_dout;

  Decoder #(.select(2)) decoder_1 (.out0(MW0), .out1(MW1), .out2(MW2), .out3(MW3), .sel(Address[25:24]), .en(MemWrite));
  Decoder #(.select(2)) decoder_2 (.out0(MR0), .out1(MR1), .out2(MR2), .out3(MR3), .sel(Address[25:24]), .en(MemRead));
  RAM #(.addrWidth(24), .asyncread("true"), .dataWidth(32)) ram_1 (
    .addr(Address[23:0]), .we(MW0), .oe(MR0), .clk(ClockIn), .din(WriteData), .dout(ram_1_dout));
  RAM #(.addrWidth(24), .asyncread("true"), .dataWidth(32)) ram_2 (
    .addr(Address[23:0]), .we(MW1), .oe(MR1), .clk(ClockIn), .din(WriteData), .dout(D1));
  RAM #(.addrWidth(24), .asyncread("true"), .dataWidth(32)) ram_3 (
    .addr(Address[23:0]), .we(MW2), .oe(MR2), .clk(ClockIn), .din(WriteData), .dout(D2));
  RAM #(.addrWidth(24), .asyncread("true"), .dataWidth(32)) ram_4 (
    .addr(Address[23:0]), .we(MW3), .oe(MR3), .clk(ClockIn), .din(WriteData), .dout(D3));
  Multiplexer #(.enable("false"), .select(2), .width(32)) multiplexer_1 (
    .in0(ram_1_dout), .in1(D1), .in2(D2), .in3(D3), .out(ReadData), .sel(Address[25:24]));

  // Other names for the same wires on the sheet: ADR_0_23[23:0] = Address[23:0]; Clock = ClockIn;
  //   WD[31:0] = WriteData
endmodule

module InstructionMemory (
  input  [23:0] Address,
  input  ClockIn,
  output [31:0] Instruction
);

  RAM #(.addrWidth(24), .asyncread("true"), .dataWidth(32)) ram_1 (
    .addr(Address), .clk(ClockIn), .dout(Instruction));  // open: we, oe, din
endmodule
